// Logisim project mar.circ as structural Verilog
module main (
);

  wire button_1_out, button_2_out, button_3_out, button_4_out, button_5_out, button_6_out, button_7_out,
       button_8_out, button_9_out, button_10_out, button_11_out, button_12_out, button_13_out, button_14_out,
       button_15_out, button_16_out, clock_1_out, controlunit_1_cr, demultiplexer_1_out1,
       demultiplexer_1_out2, demultiplexer_1_out3, demultiplexer_1_out4, demultiplexer_1_out5,
       demultiplexer_1_out6, demultiplexer_1_out7;
  wire [1:0] controlunit_1_a0, controlunit_1_mw;
  wire [2:0] controlunit_1_p0, controlunit_1_p3;
  wire [3:0] multiplexer_1_out, multiplexer_1_out_2, multiplexer_1_out_3, multiplexer_1_out_4,
       testkeyboard_1_keyout;
  wire [7:0] cyclecount_1_t0;
  wire [11:0] MAR_q;
  wire [15:0] AC_q, alu_1_aco, InReg_q, IR_q, MBR_q, outReg_q, ram_1_dout, undriven;

  Clock clock_1 (.out(clock_1_out));
  Demultiplexer #(.select(3)) demultiplexer_1 (
    .out1(demultiplexer_1_out1), .out2(demultiplexer_1_out2), .out3(demultiplexer_1_out3),
    .out4(demultiplexer_1_out4), .out5(demultiplexer_1_out5), .out6(demultiplexer_1_out6),
    .out7(demultiplexer_1_out7), .in(1'b1), .sel(controlunit_1_p3));  // open: out0
  Button button_1 (.out(button_1_out));
  Button button_2 (.out(button_2_out));
  Button button_3 (.out(button_3_out));
  Button button_4 (.out(button_4_out));
  Button button_5 (.out(button_5_out));
  Button button_6 (.out(button_6_out));
  Button button_7 (.out(button_7_out));
  Button button_8 (.out(button_8_out));
  Button button_9 (.out(button_9_out));
  Button button_10 (.out(button_10_out));
  Button button_11 (.out(button_11_out));
  Button button_12 (.out(button_12_out));
  Button button_13 (.out(button_13_out));
  Button button_14 (.out(button_14_out));
  Button button_15 (.out(button_15_out));
  Button button_16 (.out(button_16_out));
  RAM #(.addrWidth(12), .dataWidth(16)) ram_1 (
    .addr(MAR_q), .we(controlunit_1_mw[0]), .oe(controlunit_1_mw[1]), .clk(clock_1_out),
    .din({multiplexer_1_out_4, multiplexer_1_out_3, multiplexer_1_out_2, multiplexer_1_out}),
    .dout(ram_1_dout));
  testkeyboard testkeyboard_1 (
    .b0(button_1_out), .b1(button_2_out), .b2(button_3_out), .b3(button_4_out), .b4(button_5_out),
    .b5(button_6_out), .b6(button_7_out), .b7(button_8_out), .b8(button_9_out), .b9(button_10_out),
    .bA(button_11_out), .bB(button_12_out), .bC(button_13_out), .bD(button_14_out), .bE(button_15_out),
    .bF(button_16_out), .keyout(testkeyboard_1_keyout));
  Register #(.width(12)) MAR (.D(12'h5), .en(demultiplexer_1_out1), .clk(clock_1_out), .Q(MAR_q));  // open: clr
  Register #(.width(12)) PC (.en(demultiplexer_1_out2), .clk(clock_1_out));  // open: D, Q, clr
  Register #(.width(16)) MBR (.en(demultiplexer_1_out3), .clk(clock_1_out), .Q(MBR_q));  // open: D, clr
  Register #(.width(16)) AC (.D(alu_1_aco), .en(demultiplexer_1_out4), .clk(clock_1_out), .Q(AC_q));  // open: clr
  Register #(.width(16)) InReg (.en(demultiplexer_1_out5), .clk(clock_1_out), .Q(InReg_q));  // open: D, clr
  Register #(.width(16)) outReg (.en(demultiplexer_1_out6), .clk(clock_1_out), .Q(outReg_q));  // open: D, clr
  Register #(.width(16)) IR (.en(demultiplexer_1_out7), .clk(clock_1_out), .Q(IR_q));  // open: D, clr
  ControlUnit controlunit_1 (
    .En(1'b1), .RingCounter(cyclecount_1_t0), .IRopcode(testkeyboard_1_keyout), .P0(controlunit_1_p0[0]),
    .P1(controlunit_1_p0[1]), .P2(controlunit_1_p0[2]), .P3(controlunit_1_p3[0]), .P4(controlunit_1_p3[1]),
    .P5(controlunit_1_p3[2]), .A0(controlunit_1_a0[0]), .A1(controlunit_1_a0[1]), .Cr(controlunit_1_cr),
    .Mr(controlunit_1_mw[1]), .Mw(controlunit_1_mw[0]));  // open: Lalt
  Multiplexer #(.select(3), .width(16)) multiplexer_1 (
    .in0(ram_1_dout), .in1({4'b0000, MAR_q}), .in2(undriven), .in3(MBR_q), .in4(AC_q), .in5(InReg_q),
    .in6(outReg_q), .in7(IR_q),
    .out({multiplexer_1_out_4, multiplexer_1_out_3, multiplexer_1_out_2, multiplexer_1_out}),
    .sel(controlunit_1_p0));
  ALU alu_1 (.A0(controlunit_1_a0[0]), .A1(controlunit_1_a0[1]), .ACi(AC_q), .MBR(MBR_q), .ACo(alu_1_aco));
  Hex_Digit_Display hex_digit_display_1 (.value(multiplexer_1_out_4));  // open: dp
  Hex_Digit_Display hex_digit_display_2 (.value(multiplexer_1_out_3));  // open: dp
  Hex_Digit_Display hex_digit_display_3 (.value(multiplexer_1_out_2));  // open: dp
  Hex_Digit_Display hex_digit_display_4 (.value(multiplexer_1_out));  // open: dp
  cyclecount cyclecount_1 (
    .Clock(clock_1_out), .Cr(controlunit_1_cr), .T0(cyclecount_1_t0[0]), .T1(cyclecount_1_t0[1]),
    .T2(cyclecount_1_t0[2]), .T3(cyclecount_1_t0[3]), .T4(cyclecount_1_t0[4]), .T5(cyclecount_1_t0[5]),
    .T6(cyclecount_1_t0[6]), .T7(cyclecount_1_t0[7]));
  // also tied to VCC on the sheet: {alu_1_aco[0], alu_1_aco[1], alu_1_aco[2], alu_1_aco[3], alu_1_aco[4], alu_1_aco[5], alu_1_aco[6], alu_1_aco[7], alu_1_aco[8], alu_1_aco[9], alu_1_aco[10], alu_1_aco[11], alu_1_aco[12], alu_1_aco[13], alu_1_aco[14], alu_1_aco[15]}

  // Notes on the sheet:
  //   p5 p4 p3
  //   p2 p1 p0
  //   Data Bus
endmodule

module cyclecount (
  input  Clock,
  input  Cr,
  output T0,
  output T1,
  output T2,
  output T3,
  output T4,
  output T5,
  output T6,
  output T7
);

  nor nor_1 (T0, T7, T6, T5, T4, T3, T2, T1);
  D_Flip_Flop D0 (.D(T0), .clk(Clock), .Q(T1));  // open: Qn, preset, reset
  D_Flip_Flop D1 (.D(T1), .clk(Clock), .Q(T2), .reset(Cr));  // open: Qn, preset
  D_Flip_Flop D2 (.D(T2), .clk(Clock), .Q(T3), .reset(Cr));  // open: Qn, preset
  D_Flip_Flop D3 (.D(T3), .clk(Clock), .Q(T4), .reset(Cr));  // open: Qn, preset
  D_Flip_Flop D4 (.D(T4), .clk(Clock), .Q(T5), .reset(Cr));  // open: Qn, preset
  D_Flip_Flop D5 (.D(T5), .clk(Clock), .Q(T6), .reset(Cr));  // open: Qn, preset
  D_Flip_Flop D6 (.D(T6), .clk(Clock), .Q(T7), .reset(Cr));  // open: Qn, preset

  // Notes on the sheet:
  //   clock
  //   Cr
endmodule

module testkeyboard (
  input  b0,
  input  b1,
  input  b2,
  input  b3,
  input  b4,
  input  b5,
  input  b6,
  input  b7,
  input  b8,
  input  b9,
  input  bA,
  input  bB,
  input  bC,
  input  bD,
  input  bE,
  input  bF,
  output [3:0] keyout
);

  Priority_Encoder #(.select(4)) priority_encoder_1 (
    .in0(b0), .in1(b1), .in2(b2), .in3(b3), .in4(b4), .in5(b5), .in6(b6), .in7(b7), .in8(b8), .in9(b9),
    .in10(bA), .in11(bB), .in12(bC), .in13(bD), .in14(bE), .in15(bF), .out(keyout));  // open: gs, en_out, en_in
endmodule

module ControlUnit (
  input  En,
  input  [7:0] RingCounter,
  input  [3:0] IRopcode,
  output P0,
  output P1,
  output P2,
  output P3,
  output P4,
  output P5,
  output A0,
  output A1,
  output Cr,
  output Mr,
  output Mw,
  output Lalt
);

  wire decoder_1_out0, decoder_1_out1, decoder_1_out2, decoder_1_out3, decoder_1_out4, decoder_1_out5,
       decoder_1_out6, decoder_1_out7, decoder_1_out8, decoder_1_out9, decoder_1_out10, decoder_1_out11,
       decoder_1_out12, decoder_1_out13, decoder_1_out14, decoder_1_out15;

  Decoder #(.select(4)) decoder_1 (
    .out0(decoder_1_out0), .out1(decoder_1_out1), .out2(decoder_1_out2), .out3(decoder_1_out3),
    .out4(decoder_1_out4), .out5(decoder_1_out5), .out6(decoder_1_out6), .out7(decoder_1_out7),
    .out8(decoder_1_out8), .out9(decoder_1_out9), .out10(decoder_1_out10), .out11(decoder_1_out11),
    .out12(decoder_1_out12), .out13(decoder_1_out13), .out14(decoder_1_out14), .out15(decoder_1_out15),
    .sel(IRopcode), .en(En));
  Load load_1 (
    .EN(decoder_1_out1), .RingCounter(RingCounter), .P0(P0), .P1(P1), .P2(P2), .P3(P3), .P4(P4), .P5(P5),
    .A0(A0), .A1(A1), .Cr(Cr), .Mr(Mr), .Mw(Mw), .Lalt(Lalt));
  BaseOp baseop_1 (
    .EN(decoder_1_out2), .RingCounter(RingCounter), .P0(P0), .P1(P1), .P2(P2), .P3(P3), .P4(P4), .P5(P5),
    .A0(A0), .A1(A1), .Cr(Cr), .Mr(Mr), .Mw(Mw), .Lalt(Lalt));
  Add add_1 (
    .En(decoder_1_out3), .RingCounter(RingCounter), .P0(P0), .P1(P1), .P2(P2), .P3(P3), .P4(P4), .P5(P5),
    .A0(A0), .A1(A1), .Cr(Cr), .Mr(Mr), .Mw(Mw), .Lalt(Lalt));
  BaseOp baseop_2 (
    .EN(decoder_1_out4), .RingCounter(RingCounter), .P0(P0), .P1(P1), .P2(P2), .P3(P3), .P4(P4), .P5(P5),
    .A0(A0), .A1(A1), .Cr(Cr), .Mr(Mr), .Mw(Mw), .Lalt(Lalt));
  BaseOp baseop_3 (
    .EN(decoder_1_out5), .RingCounter(RingCounter), .P0(P0), .P1(P1), .P2(P2), .P3(P3), .P4(P4), .P5(P5),
    .A0(A0), .A1(A1), .Cr(Cr), .Mr(Mr), .Mw(Mw), .Lalt(Lalt));
  BaseOp baseop_4 (
    .EN(decoder_1_out6), .RingCounter(RingCounter), .P0(P0), .P1(P1), .P2(P2), .P3(P3), .P4(P4), .P5(P5),
    .A0(A0), .A1(A1), .Cr(Cr), .Mr(Mr), .Mw(Mw), .Lalt(Lalt));
  BaseOp baseop_5 (
    .EN(decoder_1_out7), .RingCounter(RingCounter), .P0(P0), .P1(P1), .P2(P2), .P3(P3), .P4(P4), .P5(P5),
    .A0(A0), .A1(A1), .Cr(Cr), .Mr(Mr), .Mw(Mw), .Lalt(Lalt));
  BaseOp baseop_6 (
    .EN(decoder_1_out8), .RingCounter(RingCounter), .P0(P0), .P1(P1), .P2(P2), .P3(P3), .P4(P4), .P5(P5),
    .A0(A0), .A1(A1), .Cr(Cr), .Mr(Mr), .Mw(Mw), .Lalt(Lalt));
  BaseOp baseop_7 (
    .EN(decoder_1_out9), .RingCounter(RingCounter), .P0(P0), .P1(P1), .P2(P2), .P3(P3), .P4(P4), .P5(P5),
    .A0(A0), .A1(A1), .Cr(Cr), .Mr(Mr), .Mw(Mw), .Lalt(Lalt));
  BaseOp baseop_8 (
    .EN(decoder_1_out10), .RingCounter(RingCounter), .P0(P0), .P1(P1), .P2(P2), .P3(P3), .P4(P4), .P5(P5),
    .A0(A0), .A1(A1), .Cr(Cr), .Mr(Mr), .Mw(Mw), .Lalt(Lalt));
  BaseOp baseop_9 (
    .EN(decoder_1_out11), .RingCounter(RingCounter), .P0(P0), .P1(P1), .P2(P2), .P3(P3), .P4(P4), .P5(P5),
    .A0(A0), .A1(A1), .Cr(Cr), .Mr(Mr), .Mw(Mw), .Lalt(Lalt));
  BaseOp baseop_10 (
    .EN(decoder_1_out12), .RingCounter(RingCounter), .P0(P0), .P1(P1), .P2(P2), .P3(P3), .P4(P4), .P5(P5),
    .A0(A0), .A1(A1), .Cr(Cr), .Mr(Mr), .Mw(Mw), .Lalt(Lalt));
  BaseOp baseop_11 (
    .EN(decoder_1_out13), .RingCounter(RingCounter), .P0(P0), .P1(P1), .P2(P2), .P3(P3), .P4(P4), .P5(P5),
    .A0(A0), .A1(A1), .Cr(Cr), .Mr(Mr), .Mw(Mw), .Lalt(Lalt));
  BaseOp baseop_12 (
    .EN(decoder_1_out14), .RingCounter(RingCounter), .P0(P0), .P1(P1), .P2(P2), .P3(P3), .P4(P4), .P5(P5),
    .A0(A0), .A1(A1), .Cr(Cr), .Mr(Mr), .Mw(Mw), .Lalt(Lalt));
  BaseOp baseop_13 (
    .EN(decoder_1_out15), .RingCounter(RingCounter), .P0(P0), .P1(P1), .P2(P2), .P3(P3), .P4(P4), .P5(P5),
    .A0(A0), .A1(A1), .Cr(Cr), .Mr(Mr), .Mw(Mw), .Lalt(Lalt));

  // Notes on the sheet:
  //   P0
  //   P1
  //   P2
  //   P3
  //   P4
  //   P5
  //   A0
  //   A1
  //   Cr
  //   Mr
  //   Mw
  //   Lalt
endmodule

module Add (
  input  En,
  input  [7:0] RingCounter,
  output P0,
  output P1,
  output P2,
  output P3,
  output P4,
  output P5,
  output A0,
  output A1,
  output Cr,
  output Mr,
  output Mw,
  output Lalt
);

  and and_1 (P0, RingCounter[3], En);
  and and_2 (Mr, RingCounter[4], En);
  and and_3 (A0, En, RingCounter[5]);
  or out3 (P3, P0, Mr);

  assign A1 = 1'b0;
  assign Cr = A0;
  assign Lalt = A0;
  assign Mw = 1'b0;
  assign P1 = P0;
  assign P2 = P0;
  assign P4 = Mr;
  assign P5 = A0;

  // Notes on the sheet:
  //   ADD=0011
endmodule

module BaseOp (
  input  EN,
  input  [7:0] RingCounter,
  output P0,
  output P1,
  output P2,
  output P3,
  output P4,
  output P5,
  output A0,
  output A1,
  output Cr,
  output Mr,
  output Mw,
  output Lalt
);
endmodule

module Load (
  input  EN,
  input  [7:0] RingCounter,
  output P0,
  output P1,
  output P2,
  output P3,
  output P4,
  output P5,
  output A0,
  output A1,
  output Cr,
  output Mr,
  output Mw,
  output Lalt
);

  // AND_Gate and_1 has open pins: in0=RingCounter[5], in1=EN, out=open
  // AND_Gate and_2 has open pins: in0=RingCounter[4], in1=EN, out=open
  // AND_Gate and_3 has open pins: in0=RingCounter[3], in1=EN, out=open
endmodule

module ALU (
  input  [15:0] ACi,
  input  [15:0] MBR,
  input  A0,
  input  A1,
  output [15:0] ACo
);

  wire comparator_1_eq, comparator_1_gt, comparator_1_lt, controlled_buffer_1_out, controlled_buffer_2_out,
       or_1_out;
  wire [15:0] adder_1_out, subtractor_1_out;

  or or_1 (or_1_out, A1, A0);
  assign controlled_buffer_1_out = or_1_out ? A1 : 1'bz;  // Controlled_Buffer controlled_buffer_1
  Comparator #(.width(1)) comparator_1 (
    .a(controlled_buffer_1_out), .b(controlled_buffer_2_out), .gt(comparator_1_gt), .eq(comparator_1_eq),
    .lt(comparator_1_lt));
  assign controlled_buffer_2_out = or_1_out ? A0 : 1'bz;  // Controlled_Buffer controlled_buffer_2
  assign ACo = comparator_1_gt ? adder_1_out : 16'bz;  // Controlled_Buffer controlled_buffer_3
  Adder #(.width(16)) adder_1 (.a(ACi), .b(MBR), .out(adder_1_out));  // open: cin, cout
  assign ACo = comparator_1_lt ? subtractor_1_out : 16'bz;  // Controlled_Buffer controlled_buffer_4
  Subtractor #(.width(16)) subtractor_1 (.a(ACi), .b(MBR), .out(subtractor_1_out));  // open: bin, bout
  assign ACo = comparator_1_eq ? {16{1'b0}} : 16'bz;  // Controlled_Buffer controlled_buffer_5
endmodule
